# Fritzing sketch Sketch (saved by Fritzing 0.9.3b)
breadboards: 2

parts:
  IC1 = L293D [package=THT]
  U2 = LuaNode32 / ESP32 [part_number=ESP32S-PIN30]
  M1 = DC Motor
  C1 = Electrolytic Capacitor [capacitance=1µF package="100 mil [THT, electrolytic]"]
  C2 = Electrolytic Capacitor [capacitance=1µF package="100 mil [THT, electrolytic]"]
  M2 = DC Motor
  U3 = Voltage Regulator - 5V [package="TO220 [THT]"]
  VCC1 = Battery
  C3 = Electrolytic Capacitor [capacitance=1µF package="100 mil [THT, electrolytic]"]

nets:
  N1: IC1.Enable_1, U2.D13
  N2: IC1.In_1, U2.D14
  N3: IC1.Out_1_(_Controlled_by_Enable_1_), M1.pin_2, C1.-
  GND: IC1.0V, U2.GND, U3.GND, VCC1.-, C3.+
  N4: IC1.Out_2_(_Controlled_by_Enable_1_), M1.pin_1, C1.+
  N5: IC1.In_2, U2.D27
  N6: IC1.+Vmotor, IC1.+V, U2.Vin, U3.output_voltage, C3.-
  N7: IC1.Out_3_(_Controlled_by_Enable_2_), C2.+, M2.pin_1
  N8: IC1.Out_4_(_Controlled_by_Enable_2_), C2.-, M2.pin_2
  N9: U3.input_voltage, VCC1.+

custom parts:
  LuaNode32 / ESP32: New Image for LuaNode32 DOIT ESP32 DEVKIT V1. Base parts from LuaNode32 / ESP32 ESP32 based LuaNode32 by G.Noorlander DOIT Esp32 DevKit v1 (30 pins long, 11 pins width) by Werner Rothschopf (modified by vanepp Dec 2018)
